// Logisim project Ctl_Conditional.circ as structural Verilog: 1 circuit, main circuit Conditional
module Conditional (
  input  Enable,
  input  [15:0] Instruction,
  input  Z,
  input  C,
  input  N,
  input  V,
  output Verified,
  output [10:0] Offset
);

  wire CC_LO, CS_HS, GE, GT, HI, LE, LS, LT, MI, multiplexer_1_out, NE, or_1_out, PL, VC, VS;
  wire [10:0] bit_extender_1_out, multiplexer_2_out;

  Multiplexer #(.select(4)) multiplexer_1 (
    .in0(Z), .in1(NE), .in2(CS_HS), .in3(CC_LO), .in4(MI), .in5(PL), .in6(VS), .in7(VC), .in8(HI), .in9(LS),
    .in10(GE), .in11(LT), .in12(GT), .in13(LE), .in14(1'b1), .out(multiplexer_1_out), .sel(Instruction[11:8]));  // open: in15
  // Probe on Instruction[11:8]
  not not_1 (NE, Z);
  and and_1 (CS_HS, C, 1'b1);
  xnor xnor_1 (CC_LO, C, 1'b0);
  or or_1 (or_1_out, multiplexer_1_out, Instruction[13]);
  assign bit_extender_1_out = {{3{Instruction[7]}}, Instruction[7:0]};  // Bit_Extender bit_extender_1
  Multiplexer #(.width(11)) multiplexer_2 (
    .in0(bit_extender_1_out), .in1(Instruction[10:0]), .out(multiplexer_2_out), .sel(Instruction[13]));
  and and_2 (Verified, or_1_out, Enable);
  Multiplexer #(.width(11)) multiplexer_3 (.in0({11{1'b0}}), .in1(multiplexer_2_out), .out(Offset), .sel(Verified));
  and and_3 (GT, GE, NE);
  and and_4 (MI, N, 1'b1);
  xnor xnor_2 (PL, N, 1'b0);
  and and_5 (VS, V, 1'b1);
  xnor xnor_3 (VC, V, 1'b0);
  or or_2 (LE, Z, LT);
  and and_6 (HI, CS_HS, NE);
  or or_3 (LS, CC_LO, Z);
  xnor xnor_4 (GE, N, V);
  not not_2 (LT, GE);

  // Other names for the same wires on the sheet: EQ = Z; imm8[7:0] = Instruction[7:0];
  //   imm11[10:0] = Instruction[10:0]; cond[3:0] = Instruction[11:8]; incond = Instruction[13]
endmodule
