// Logisim project Ctl_Data_Processing.circ as structural Verilog: 1 circuit, main circuit Data_Processing
module Data_Processing (
  input  Enable,
  input  [15:0] Instruction,
  output [2:0] Rd,
  output [2:0] Rn,
  output [2:0] Rm,
  output [3:0] ALU_Opcode,
  output [3:0] Flags_Update_Mask
);

  wire [3:0] multiplexer_1_out;

  Multiplexer #(.select(4), .width(4)) multiplexer_1 (
    .in0(4'b1110), .in1(4'b1110), .in2(4'b1110), .in3(4'b1110), .in4(4'b1110), .in5(4'b1111), .in6(4'b1111),
    .in7(4'b1110), .in8(4'b1110), .in9(4'b1111), .in10(4'b1111), .in11(4'b1111), .in12(4'b1110),
    .in13(4'b1100), .in14(4'b1110), .in15(4'b1110), .out(multiplexer_1_out), .sel(Instruction[9:6]));
  Pull_Resistor pull_resistor_1 (.node(Rd));
  assign Rd = Enable ? Instruction[2:0] : 3'bz;  // Controlled_Buffer controlled_buffer_1
  Pull_Resistor pull_resistor_2 (.node(Rn));
  assign Rn = Enable ? Instruction[2:0] : 3'bz;  // Controlled_Buffer controlled_buffer_2
  Pull_Resistor pull_resistor_3 (.node(Rm));
  assign Rm = Enable ? Instruction[5:3] : 3'bz;  // Controlled_Buffer controlled_buffer_3
  Pull_Resistor pull_resistor_4 (.node(ALU_Opcode));
  assign ALU_Opcode = Enable ? Instruction[9:6] : 4'bz;  // Controlled_Buffer controlled_buffer_4
  Pull_Resistor pull_resistor_5 (.node(Flags_Update_Mask));
  assign Flags_Update_Mask = Enable ? multiplexer_1_out : 4'bz;  // Controlled_Buffer controlled_buffer_5

  // Other names for the same wires on the sheet: Rd_t[2:0] = Instruction[2:0]; Rn_t[2:0] = Instruction[2:0];
  //   Rm_t[2:0] = Instruction[5:3]; ALU_Opcode_t[3:0] = Instruction[9:6]

  // Notes on the sheet:
  //   Note 2: RSB instruction has Rn as 1st operand.
  //   MUL instruction has Rn as 1st operand and Rdm as 2nd operand
  //   For simplification purposes, Rm is used for 1st operand both here and in the ALU.
  //   Note: instructions that does not save the result will still have the second operand as the destination register, the ALU will copy the second register to the destination register
  //   Pull output low on Enable = 0
endmodule
