// Logisim project Ctl_SP_Address.circ as structural Verilog: 1 circuit, main circuit SP_Address
module SP_Address (
  input  [31:0] Stack_Pointer,
  input  [15:0] Instruction,
  input  Enable,
  output [31:0] New_Stack_Pointer,
  output Write_Enable
);

  wire add_or_sub;
  wire [6:0] imm7;
  wire [15:0] bit_extender_1_out;
  wire [15:8] and_1_out;
  wire [31:0] ADD, bit_extender_2_out, bit_extender_3_out, bit_extender_4_out, newSP, SUB;

  assign bit_extender_1_out = {{15{Enable}}, Enable};  // Bit_Extender bit_extender_1
  assign {and_1_out, add_or_sub, imm7} = Instruction & bit_extender_1_out;  // AND_Gate and_1, 16 bits wide
  assign bit_extender_2_out = {{31{Enable}}, Enable};  // Bit_Extender bit_extender_2
  assign New_Stack_Pointer = newSP & bit_extender_2_out;  // AND_Gate and_2, 32 bits wide
  assign bit_extender_3_out = {{25{1'b0}}, imm7};  // Bit_Extender bit_extender_3
  assign bit_extender_4_out = {{25{1'b0}}, imm7};  // Bit_Extender bit_extender_4
  Adder #(.width(32)) adder_1 (.a(bit_extender_3_out), .b(Stack_Pointer), .out(ADD));  // open: cin, cout
  Subtractor #(.width(32)) subtractor_1 (.a(Stack_Pointer), .b(bit_extender_4_out), .out(SUB));  // open: bin, bout
  Multiplexer #(.width(32)) multiplexer_1 (.in0(ADD), .in1(SUB), .out(newSP), .sel(add_or_sub));

  assign Write_Enable = Enable;

  // Other names for the same wires on the sheet: SP[31:0] = Stack_Pointer

  // Notes on the sheet:
  //   Pull output low on Enable = 0
endmodule
