// Logisim project Ctl_Shift_Add_Sub_Mov.circ as structural Verilog: 3 circuits, main circuit FLAGS_MODULE
module Shift_Add_Sub_Mov (
  input  Enable,
  input  [15:0] Instruction,
  output [3:0] Flags_Update_Mask,
  output Imm32_Enable,
  output [2:0] Rm,
  output [31:0] Imm32,
  output [2:0] Rd,
  output [3:0] ALU_Opcode,
  output Carry,
  output [4:0] Imm5,
  output [2:0] Rn
);

  wire and_1_out, and_2_out, and_3_out, comparator_1_eq, or_1_out;
  wire [2:0] multiplexer_1_out, multiplexer_4_out;
  wire [3:0] alu_opcode_module_1_out_2, alu_opcode_module_1_out_3, flags_module_1_out_2, multiplexer_5_out;
  wire [4:0] bitselector_2_out;
  wire [8:0] bitselector_1_out;
  wire [31:0] bit_extender_1_out, bit_extender_2_out, multiplexer_2_out, multiplexer_3_out, negator_1_out;

  BitSelector #(.group(9), .width(16)) bitselector_1 (.in(Instruction), .out(bitselector_1_out), .sel(1'b1));
  BitSelector #(.group(5), .width(9)) bitselector_2 (.in(bitselector_1_out), .out(bitselector_2_out), .sel(1'b0));
  and and_1 (and_1_out, ~Instruction[11], ~Instruction[12]);  // AND_Gate
  assign bit_extender_1_out = {{24{1'b0}}, Instruction[7:0]};  // Bit_Extender bit_extender_1
  and and_2 (and_2_out, Instruction[11], Instruction[12]);
  Multiplexer #(.width(3)) multiplexer_1 (
    .in0(Instruction[5:3]), .in1(Instruction[8:6]), .out(multiplexer_1_out), .sel(and_2_out));
  assign bit_extender_2_out = {{29{1'b0}}, Instruction[8:6]};  // Bit_Extender bit_extender_2
  Multiplexer #(.width(32)) multiplexer_2 (
    .in0(bit_extender_1_out), .in1(negator_1_out), .out(multiplexer_2_out), .sel(and_1_out));
  Negator #(.width(32)) negator_1 (.in(bit_extender_1_out), .out(negator_1_out));
  ALU_OPCODE_MODULE alu_opcode_module_1 (
    .in_1(Instruction), .out_2(alu_opcode_module_1_out_2), .out_3(alu_opcode_module_1_out_3));
  FLAGS_MODULE flags_module_1 (.in_1(bitselector_2_out), .out_2(flags_module_1_out_2));
  and and_3 (and_3_out, Instruction[10], Instruction[11], Instruction[12]);
  Multiplexer #(.width(32)) multiplexer_3 (
    .in0(bit_extender_2_out), .in1(multiplexer_2_out), .out(multiplexer_3_out), .sel(Instruction[13]));
  Multiplexer #(.width(3)) multiplexer_4 (
    .in0(Instruction[2:0]), .in1(Instruction[10:8]), .out(multiplexer_4_out), .sel(Instruction[13]));
  Multiplexer #(.width(4)) multiplexer_5 (
    .in0(alu_opcode_module_1_out_2), .in1(alu_opcode_module_1_out_3), .out(multiplexer_5_out),
    .sel(Instruction[13]));
  or or_1 (or_1_out, and_3_out, Instruction[13]);
  Comparator #(.mode("unsigned"), .width(4)) comparator_1 (
    .a(4'b0110), .b(multiplexer_5_out), .eq(comparator_1_eq));  // open: gt, lt
  Multiplexer #(.width(4)) multiplexer_6 (
    .in0(4'b0000), .in1(flags_module_1_out_2), .out(Flags_Update_Mask), .sel(Enable));
  Multiplexer multiplexer_7 (.in0(1'b0), .in1(or_1_out), .out(Imm32_Enable), .sel(Enable));
  Multiplexer #(.width(3)) multiplexer_8 (.in0(3'b000), .in1(multiplexer_1_out), .out(Rm), .sel(Enable));
  Multiplexer #(.width(32)) multiplexer_9 (.in0({32{1'b0}}), .in1(multiplexer_3_out), .out(Imm32), .sel(Enable));
  Multiplexer #(.width(3)) multiplexer_10 (.in0(3'b000), .in1(multiplexer_4_out), .out(Rd), .sel(Enable));
  Multiplexer #(.width(4)) multiplexer_11 (.in0(4'b0000), .in1(multiplexer_5_out), .out(ALU_Opcode), .sel(Enable));
  Multiplexer multiplexer_12 (.in0(1'b0), .in1(comparator_1_eq), .out(Carry), .sel(Enable));
  Multiplexer #(.width(5)) multiplexer_13 (.in0({5{1'b0}}), .in1(Instruction[10:6]), .out(Imm5), .sel(Enable));
  Multiplexer #(.width(3)) multiplexer_14 (.in0(3'b000), .in1(Instruction[5:3]), .out(Rn), .sel(Enable));
endmodule

module FLAGS_MODULE (
  input  [4:0] in_1,
  output [3:0] out_2
);

  wire and_1_out, and_2_out, and_3_out, not_1_out;

  not not_1 (not_1_out, in_1[4]);
  or or_1 (out_2[2], not_1_out, in_1[2], in_1[3]);
  and and_1 (and_1_out, in_1[3], in_1[3]);
  and and_2 (and_2_out, in_1[3], in_1[4]);
  and and_3 (and_3_out, in_1[3], in_1[4]);
  or or_2 (out_2[3], and_1_out, and_2_out, and_3_out);

  assign out_2[1:0] = 2'b11;
endmodule

module ALU_OPCODE_MODULE (
  input  [15:0] in_1,
  output [3:0] out_2,
  output [3:0] out_3
);

  wire comparator_1_eq, comparator_2_gt;
  wire [3:0] adder_1_out, adder_2_out, adder_3_out, multiplexer_1_out;

  Adder #(.width(4)) adder_1 (.a(4'b0010), .b(in_1[14:11]), .out(adder_1_out));  // open: cin, cout
  Adder #(.width(4)) adder_2 (.a(adder_1_out), .b({2'b00, in_1[10:9]}), .out(adder_2_out));  // open: cin, cout
  Adder #(.width(4)) adder_3 (.a(adder_1_out), .b({3'b000, in_1[9]}), .out(adder_3_out));  // open: cin, cout
  Comparator #(.mode("unsigned"), .width(4)) comparator_1 (
    .a(adder_1_out), .b(4'b0101), .eq(comparator_1_eq));  // open: gt, lt
  Comparator #(.mode("unsigned"), .width(4)) comparator_2 (
    .a(adder_2_out), .b(4'b0110), .gt(comparator_2_gt));  // open: eq, lt
  Multiplexer #(.width(4)) multiplexer_1 (
    .in0(adder_2_out), .in1(adder_3_out), .out(multiplexer_1_out), .sel(comparator_2_gt));
  Multiplexer #(.width(4)) multiplexer_2 (
    .in0(adder_1_out), .in1(multiplexer_1_out), .out(out_3), .sel(comparator_1_eq));

  assign out_2 = {in_1[13:11], 1'b1};
endmodule
